# Fritzing sketch schematics (saved by Fritzing 0.9.3b)
breadboards: 1

parts:
  U1 = TMP01 - Low Power, Programmable Temperature Controller [part_number=TMP01]
  Composant1 = Arduino Uno (Rev3)
  R2 = Photocell (LDR) [package=THT]
  R3 = Resistor [tolerance=±5% resistance=3.3k package="1206 [SMD]"]
  Composant2 = Soil Moisture Sensor
  Composant3 = Arduino Ethernet Shield (Rev3)
  PIR_Sensor = LHi958 [package=to-39]

nets:
  N1: U1.10V, Composant1.A4/SDA
  N2: U1.5V, Composant1.A5/SCL
  GND: U1.COMMON, U1.STROBE, U1.VBG, U1.CAP, Composant1.GND, R2.pin_1, Composant2.GND, PIR_Sensor.GND
  N3: U1.V+, Composant1.3V3
  N4: Composant1.A0, R2.pin_0, R3.Pin_1
  N5: Composant1.A1, Composant2.SIG
  5V: Composant1.5V, R3.Pin_0, Composant2.VCC, PIR_Sensor.D
  N6: Composant3.D2, PIR_Sensor.n.a.
